// Logisim project ep16cpu.circ as structural Verilog: 3 circuits, main circuit main
module main (
);

  wire Aload, ALUwrite, and_1_out, and_2_out, and_3_out, Bload, Clk, FlagWr, HMload, IRload, LMload, MEMdisa,
       not_1_out, not_2_out, not_3_out, not_4_out, not_5_out, PCincr, PCload, RAMwrite, TTYread, TTYwrite;
  wire [1:0] MAmux;
  wire [2:0] ALUop;
  wire [3:0] NZVC;
  wire [6:0] rom_1_data;
  wire [7:0] A_q, ALU_output, B_q, keyboard_1_data;
  wire [7:3] Opcode;
  wire [7:7] rom_1_data_2;
  wire [15:0] MAR, MARidx, multiplexer_1_out, PC_q;
  wire [15:15] Control_ctrllines;

  Counter #(.width(16), .max('hffff)) PC (
    .load(PCload), .D(multiplexer_1_out), .count(PCincr), .Q(PC_q), .clk(Clk));  // open: carry, clr
  Control Control (
    .NZVC(NZVC), .Opcode({Opcode, ALUop}),
    .CtrlLines({Control_ctrllines[15], MAmux, FlagWr, MEMdisa, TTYwrite, TTYread, ALUwrite, Bload, Aload, LMload, HMload, IRload, RAMwrite, PCincr, PCload}),
    .Clk(Clk));
  Multiplexer #(.select(2), .width(16), .enable("false")) multiplexer_1 (
    .in0(PC_q), .in1(MAR), .in2(MARidx), .out(multiplexer_1_out), .sel(MAmux));  // open: in3
  // Probe on multiplexer_1_out
  not not_1 (not_1_out, multiplexer_1_out[15]);
  not not_2 (not_2_out, MEMdisa);
  not not_3 (not_3_out, MEMdisa);
  and and_1 (and_1_out, not_1_out, not_2_out);
  not not_4 (not_4_out, RAMwrite);
  and and_2 (and_2_out, multiplexer_1_out[15], not_3_out);
  ROM #(.addrWidth(15)) rom_1 (.addr(multiplexer_1_out[14:0]), .data({rom_1_data_2[7], rom_1_data}), .sel(and_1_out));
  RAM #(.addrWidth(15)) ram_1 (
    .addr(multiplexer_1_out[14:0]), .data({rom_1_data_2[7], rom_1_data}), .sel(and_2_out), .clk(Clk),
    .ld(not_4_out));  // open: clr
  // Probe on rom_1_data
  TTY tty_1 (.data(rom_1_data), .clk(Clk), .we(TTYwrite));  // open: clr
  Register IR (.D({rom_1_data_2[7], rom_1_data}), .en(IRload), .Q({Opcode, ALUop}), .clk(Clk));  // open: clr
  // Probe on {Opcode, ALUop}
  not not_5 (not_5_out, Clk);
  and and_3 (and_3_out, not_5_out, TTYread);
  // Probe on {rom_1_data_2[7], rom_1_data}
  Register HMAR (.D({rom_1_data_2[7], rom_1_data}), .en(HMload), .Q(MAR[15:8]), .clk(Clk));  // open: clr
  Keyboard #(.buflen(80)) keyboard_1 (
    .clk(Clk), .re(and_3_out), .avail(keyboard_1_data[7]), .data(keyboard_1_data[6:0]));  // open: clr
  Register LMAR (.D({rom_1_data_2[7], rom_1_data}), .en(LMload), .Q(MAR[7:0]), .clk(Clk));  // open: clr
  // Probe on MAR
  // Probe on keyboard_1_data
  assign {rom_1_data_2[7], rom_1_data} = TTYread ? keyboard_1_data : 8'bz;  // Controlled_Buffer controlled_buffer_1
  Register A (.D({rom_1_data_2[7], rom_1_data}), .en(Aload), .Q(A_q), .clk(Clk));  // open: clr
  Register B (.D({rom_1_data_2[7], rom_1_data}), .en(Bload), .Q(B_q), .clk(Clk));  // open: clr
  // Probe on A_q
  // Probe on B_q
  Adder #(.width(16)) adder_1 (.a({{8{1'b0}}, B_q}), .b(MAR), .out(MARidx), .cin(1'b0));  // open: cout
  assign {rom_1_data_2[7], rom_1_data} = ALUwrite ? ALU_output : 8'bz;  // Controlled_Buffer controlled_buffer_2
  ALU ALU (.NZVC(NZVC), .Op(ALUop), .Arg1(A_q), .Output(ALU_output), .Arg2(B_q), .FlagWr(FlagWr), .Clk(Clk));
  // Probe on ALUop
  // Probe on NZVC
  // Probe on ALU_output

  // Other names for the same wires on the sheet: Opcode[2:0] = ALUop

  // Notes on the sheet:
  //   ROM
  //   RAM
  //   contents of rom_1 (hex, n*v repeats v):
  //   e 1 1d 80 0 1d 80 1 15 80 0 16 80 1 0 1f 0 5d 1d 80 2 f c8 9 22 0 22 e 32 25 6 5 0 32 f 64 9 17 0 2f
  //   e 31 25 6 5 0 32 f 20 26 f 30 1e 80 3 f a 1 17 0 43 2f 80 3 5 0 37 16 80 3 26 f 3a 0 25 f a 26 16 80
  //   1 1e 80 0 16 80 2 1e 80 1 5 0 8 5 0 5d
  //   Terminal
  //   Keyboard
endmodule

module ALU (
  input  [2:0] Op,
  input  FlagWr,
  input  [7:0] Arg1,
  input  Clk,
  input  [7:0] Arg2,
  output [3:0] NZVC,
  output [7:0] Output
);

  wire Coutlow, Noutlow, Voutlow, Zoutlow;
  wire [7:4] rom_1_data;

  ROM #(.addrWidth(13)) rom_1 (
    .addr({Op, Arg1[7:4], Arg2[7:4], Zoutlow, Coutlow}), .data({rom_1_data, Output[7:4]}));  // open: sel
  ROM #(.addrWidth(13)) rom_2 (
    .addr({Op, Arg1[3:0], Arg2[3:0], 2'b10}), .data({Noutlow, Zoutlow, Voutlow, Coutlow, Output[3:0]}));  // open: sel
  Register #(.width(4)) Flags (.D(rom_1_data), .en(FlagWr), .Q(NZVC), .clk(Clk));  // open: clr

  // Other names for the same wires on the sheet: Arg2high[3:0] = Arg2[7:4]; Arg1high[3:0] = Arg1[7:4];
  //   Arg2low[3:0] = Arg2[3:0]; Arg1low[3:0] = Arg1[3:0]; ALUop[2:0] = Op; Resultlow[3:0] = Output[3:0]

  // Notes on the sheet:
  //   contents of rom_1 (hex, n*v repeats v):
  //   0 1 40 1 1 2 1 2 2 3 2 3 3 4 3 4 4 5 4 5 5 6 5 6 6 7 6 7 7 a8 7 a8 88 89 88 89 89 8a 89 8a 8a 8b 8a
  //   8b 8b 8c 8b 8c 8c 8d 8c 8d 8d 8e 8d 8e 8e 8f 8e 8f 8f 10 8f 50 1 2 1 2 2 3 2 3 3 4 3 4 4 5 4 5 5 6 5
  //   6 6 7 6 7 7 a8 7 a8 a8 a9 a8 a9 89 8a 89 8a 8a 8b 8a 8b 8b 8c 8b 8c 8c 8d 8c 8d 8d 8e 8d 8e 8e 8f 8e
  //   8f 8f 10 8f 50 10 11 50 11 2 3 2 3 3 4 3 4 4 5 4 5 5 6 5 6 6 7 6 7 7 a8 7 a8 a8 a9 a8 a9 a9 aa a9 aa
  //   8a 8b 8a 8b 8b 8c 8b 8c 8c 8d 8c 8d 8d 8e 8d 8e 8e 8f 8e 8f 8f 10 8f 50 10 11 50 11 11 12 11 12 3 4
  //   3 4 4 5 4 5 5 6 5 6 6 7 6 7 7 a8 7 a8 a8 a9 a8 a9 a9 aa a9 aa aa ab aa ab 8b 8c 8b 8c 8c 8d 8c 8d 8d
  //   8e 8d 8e 8e 8f 8e 8f 8f 10 8f 50 10 11 50 11 11 12 11 12 12 13 12 13 4 5 4 5 5 6 5 6 6 7 6 7 7 a8 7
  //   a8 a8 a9 a8 a9 a9 aa a9 aa aa ab aa ab ab ac ab ac 8c 8d 8c 8d 8d 8e 8d 8e 8e 8f 8e 8f 8f 10 8f 50
  //   10 11 50 11 11 12 11 12 12 13 12 13 13 14 13 14 5 6 5 6 6 7 6 7 7 a8 7 a8 a8 a9 a8 a9 a9 aa a9 aa aa
  //   ab aa ab ab ac ab ac ac ad ac ad 8d 8e 8d 8e 8e 8f 8e 8f 8f 10 8f 50 10 11 50 11 11 12 11 12 12 13
  //   12 13 13 14 13 14 14 15 14 15 6 7 6 7 7 a8 7 a8 a8 a9 a8 a9 a9 aa a9 aa aa ab aa ab ab ac ab ac ac
  //   ad ac ad ad ae ad ae 8e 8f 8e 8f 8f 10 8f 50 10 11 50 11 11 12 11 12 12 13 12 13 13 14 13 14 14 15
  //   14 15 15 16 15 16 7 a8 7 a8 a8 a9 a8 a9 a9 aa a9 aa aa ab aa ab ab ac ab ac ac ad ac ad ad ae ad ae
  //   ae af ae af 8f 10 8f 50 10 11 50 11 11 12 11 12 12 13 12 13 13 14 13 14 14 15 14 15 15 16 15 16 16
  //   17 16 17 88 89 88 89 89 8a 89 8a 8a 8b 8a 8b 8b 8c 8b 8c 8c 8d 8c 8d 8d 8e 8d 8e 8e 8f 8e 8f 8f 10
  //   8f 50 30 31 70 31 31 32 31 32 32 33 32 33 33 34 33 34 34 35 34 35 35 36 35 36 36 37 36 37 37 98 37
  //   98 89 8a 89 8a 8a 8b 8a 8b 8b 8c 8b 8c 8c 8d 8c 8d 8d 8e 8d 8e 8e 8f 8e 8f 8f 10 8f 50 10 11 50 11
  //   31 32 31 32 32 33 32 33 33 34 33 34 34 35 34 35 35 36 35 36 36 37 36 37 37 98 37 98 98 99 98 99 8a
  //   8b 8a 8b 8b 8c 8b 8c 8c 8d 8c 8d 8d 8e 8d 8e 8e 8f 8e 8f 8f 10 8f 50 10 11 50 11 11 12 11 12 32 33
  //   32 33 33 34 33 34 34 35 34 35 35 36 35 36 36 37 36 37 37 98 37 98 98 99 98 99 99 9a 99 9a 8b 8c 8b
  //   8c 8c 8d 8c 8d 8d 8e 8d 8e 8e 8f 8e 8f 8f 10 8f 50 10 11 50 11 11 12 11 12 12 13 12 13 33 34 33 34
  //   34 35 34 35 35 36 35 36 36 37 36 37 37 98 37 98 98 99 98 99 99 9a 99 9a 9a 9b 9a 9b 8c 8d 8c 8d 8d
  //   8e 8d 8e 8e 8f 8e 8f 8f 10 8f 50 10 11 50 11 11 12 11 12 12 13 12 13 13 14 13 14 34 35 34 35 35 36
  //   35 36 36 37 36 37 37 98 37 98 98 99 98 99 99 9a 99 9a 9a 9b 9a 9b 9b 9c 9b 9c 8d 8e 8d 8e 8e 8f 8e
  //   8f 8f 10 8f 50 10 11 50 11 11 12 11 12 12 13 12 13 13 14 13 14 14 15 14 15 35 36 35 36 36 37 36 37
  //   37 98 37 98 98 99 98 99 99 9a 99 9a 9a 9b 9a 9b 9b 9c 9b 9c 9c 9d 9c 9d 8e 8f 8e 8f 8f 10 8f 50 10
  //   11 50 11 11 12 11 12 12 13 12 13 13 14 13 14 14 15 14 15 15 16 15 16 36 37 36 37 37 98 37 98 98 99
  //   98 99 99 9a 99 9a 9a 9b 9a 9b 9b 9c 9b 9c 9c 9d 9c 9d 9d 9e 9d 9e 8f 10 8f 50 10 11 50 11 11 12 11
  //   12 12 13 12 13 13 14 13 14 14 15 14 15 15 16 15 16 16 17 16 17 37 98 37 98 98 99 98 99 99 9a 99 9a
  //   9a 9b 9a 9b 9b 9c 9b 9c 9c 9d 9c 9d 9d 9e 9d 9e 9e 9f 9e 9f 0 bf 40 bf bf be bf be be bd be bd bd bc
  //   bd bc bc bb bc bb bb ba bb ba ba b9 ba b9 b9 b8 b9 b8 98 17 98 17 17 16 17 16 16 15 16 15 15 14 15
  //   14 14 13 14 13 13 12 13 12 12 11 12 11 11 10 11 50 1 0 1 40 0 bf 40 bf bf be bf be be bd be bd bd bc
  //   bd bc bc bb bc bb bb ba bb ba ba b9 ba b9 99 98 99 98 98 17 98 17 17 16 17 16 16 15 16 15 15 14 15
  //   14 14 13 14 13 13 12 13 12 12 11 12 11 2 1 2 1 1 0 1 40 0 bf 40 bf bf be bf be be bd be bd bd bc bd
  //   bc bc bb bc bb bb ba bb ba 9a 99 9a 99 99 98 99 98 98 17 98 17 17 16 17 16 16 15 16 15 15 14 15 14
  //   14 13 14 13 13 12 13 12 3 2 3 2 2 1 2 1 1 0 1 40 0 bf 40 bf bf be bf be be bd be bd bd bc bd bc bc
  //   bb bc bb 9b 9a 9b 9a 9a 99 9a 99 99 98 99 98 98 17 98 17 17 16 17 16 16 15 16 15 15 14 15 14 14 13
  //   14 13 4 3 4 3 3 2 3 2 2 1 2 1 1 0 1 40 0 bf 40 bf bf be bf be be bd be bd bd bc bd bc 9c 9b 9c 9b 9b
  //   9a 9b 9a 9a 99 9a 99 99 98 99 98 98 17 98 17 17 16 17 16 16 15 16 15 15 14 15 14 5 4 5 4 4 3 4 3 3 2
  //   3 2 2 1 2 1 1 0 1 40 0 bf 40 bf bf be bf be be bd be bd 9d 9c 9d 9c 9c 9b 9c 9b 9b 9a 9b 9a 9a 99 9a
  //   99 99 98 99 98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
  //   contents of rom_2 (hex, n*v repeats v):
  //   0 1 40 1 1 2 1 2 2 3 2 3 3 4 3 4 4 5 4 5 5 6 5 6 6 7 6 7 7 a8 7 a8 88 89 88 89 89 8a 89 8a 8a 8b 8a
  //   8b 8b 8c 8b 8c 8c 8d 8c 8d 8d 8e 8d 8e 8e 8f 8e 8f 8f 10 8f 50 1 2 1 2 2 3 2 3 3 4 3 4 4 5 4 5 5 6 5
  //   6 6 7 6 7 7 a8 7 a8 a8 a9 a8 a9 89 8a 89 8a 8a 8b 8a 8b 8b 8c 8b 8c 8c 8d 8c 8d 8d 8e 8d 8e 8e 8f 8e
  //   8f 8f 10 8f 50 10 11 50 11 2 3 2 3 3 4 3 4 4 5 4 5 5 6 5 6 6 7 6 7 7 a8 7 a8 a8 a9 a8 a9 a9 aa a9 aa
  //   8a 8b 8a 8b 8b 8c 8b 8c 8c 8d 8c 8d 8d 8e 8d 8e 8e 8f 8e 8f 8f 10 8f 50 10 11 50 11 11 12 11 12 3 4
  //   3 4 4 5 4 5 5 6 5 6 6 7 6 7 7 a8 7 a8 a8 a9 a8 a9 a9 aa a9 aa aa ab aa ab 8b 8c 8b 8c 8c 8d 8c 8d 8d
  //   8e 8d 8e 8e 8f 8e 8f 8f 10 8f 50 10 11 50 11 11 12 11 12 12 13 12 13 4 5 4 5 5 6 5 6 6 7 6 7 7 a8 7
  //   a8 a8 a9 a8 a9 a9 aa a9 aa aa ab aa ab ab ac ab ac 8c 8d 8c 8d 8d 8e 8d 8e 8e 8f 8e 8f 8f 10 8f 50
  //   10 11 50 11 11 12 11 12 12 13 12 13 13 14 13 14 5 6 5 6 6 7 6 7 7 a8 7 a8 a8 a9 a8 a9 a9 aa a9 aa aa
  //   ab aa ab ab ac ab ac ac ad ac ad 8d 8e 8d 8e 8e 8f 8e 8f 8f 10 8f 50 10 11 50 11 11 12 11 12 12 13
  //   12 13 13 14 13 14 14 15 14 15 6 7 6 7 7 a8 7 a8 a8 a9 a8 a9 a9 aa a9 aa aa ab aa ab ab ac ab ac ac
  //   ad ac ad ad ae ad ae 8e 8f 8e 8f 8f 10 8f 50 10 11 50 11 11 12 11 12 12 13 12 13 13 14 13 14 14 15
  //   14 15 15 16 15 16 7 a8 7 a8 a8 a9 a8 a9 a9 aa a9 aa aa ab aa ab ab ac ab ac ac ad ac ad ad ae ad ae
  //   ae af ae af 8f 10 8f 50 10 11 50 11 11 12 11 12 12 13 12 13 13 14 13 14 14 15 14 15 15 16 15 16 16
  //   17 16 17 88 89 88 89 89 8a 89 8a 8a 8b 8a 8b 8b 8c 8b 8c 8c 8d 8c 8d 8d 8e 8d 8e 8e 8f 8e 8f 8f 10
  //   8f 50 30 31 70 31 31 32 31 32 32 33 32 33 33 34 33 34 34 35 34 35 35 36 35 36 36 37 36 37 37 98 37
  //   98 89 8a 89 8a 8a 8b 8a 8b 8b 8c 8b 8c 8c 8d 8c 8d 8d 8e 8d 8e 8e 8f 8e 8f 8f 10 8f 50 10 11 50 11
  //   31 32 31 32 32 33 32 33 33 34 33 34 34 35 34 35 35 36 35 36 36 37 36 37 37 98 37 98 98 99 98 99 8a
  //   8b 8a 8b 8b 8c 8b 8c 8c 8d 8c 8d 8d 8e 8d 8e 8e 8f 8e 8f 8f 10 8f 50 10 11 50 11 11 12 11 12 32 33
  //   32 33 33 34 33 34 34 35 34 35 35 36 35 36 36 37 36 37 37 98 37 98 98 99 98 99 99 9a 99 9a 8b 8c 8b
  //   8c 8c 8d 8c 8d 8d 8e 8d 8e 8e 8f 8e 8f 8f 10 8f 50 10 11 50 11 11 12 11 12 12 13 12 13 33 34 33 34
  //   34 35 34 35 35 36 35 36 36 37 36 37 37 98 37 98 98 99 98 99 99 9a 99 9a 9a 9b 9a 9b 8c 8d 8c 8d 8d
  //   8e 8d 8e 8e 8f 8e 8f 8f 10 8f 50 10 11 50 11 11 12 11 12 12 13 12 13 13 14 13 14 34 35 34 35 35 36
  //   35 36 36 37 36 37 37 98 37 98 98 99 98 99 99 9a 99 9a 9a 9b 9a 9b 9b 9c 9b 9c 8d 8e 8d 8e 8e 8f 8e
  //   8f 8f 10 8f 50 10 11 50 11 11 12 11 12 12 13 12 13 13 14 13 14 14 15 14 15 35 36 35 36 36 37 36 37
  //   37 98 37 98 98 99 98 99 99 9a 99 9a 9a 9b 9a 9b 9b 9c 9b 9c 9c 9d 9c 9d 8e 8f 8e 8f 8f 10 8f 50 10
  //   11 50 11 11 12 11 12 12 13 12 13 13 14 13 14 14 15 14 15 15 16 15 16 36 37 36 37 37 98 37 98 98 99
  //   98 99 99 9a 99 9a 9a 9b 9a 9b 9b 9c 9b 9c 9c 9d 9c 9d 9d 9e 9d 9e 8f 10 8f 50 10 11 50 11 11 12 11
  //   12 12 13 12 13 13 14 13 14 14 15 14 15 15 16 15 16 16 17 16 17 37 98 37 98 98 99 98 99 99 9a 99 9a
  //   9a 9b 9a 9b 9b 9c 9b 9c 9c 9d 9c 9d 9d 9e 9d 9e 9e 9f 9e 9f 0 bf 40 bf bf be bf be be bd be bd bd bc
  //   bd bc bc bb bc bb bb ba bb ba ba b9 ba b9 b9 b8 b9 b8 98 17 98 17 17 16 17 16 16 15 16 15 15 14 15
  //   14 14 13 14 13 13 12 13 12 12 11 12 11 11 10 11 50 1 0 1 40 0 bf 40 bf bf be bf be be bd be bd bd bc
  //   bd bc bc bb bc bb bb ba bb ba ba b9 ba b9 99 98 99 98 98 17 98 17 17 16 17 16 16 15 16 15 15 14 15
  //   14 14 13 14 13 13 12 13 12 12 11 12 11 2 1 2 1 1 0 1 40 0 bf 40 bf bf be bf be be bd be bd bd bc bd
  //   bc bc bb bc bb bb ba bb ba 9a 99 9a 99 99 98 99 98 98 17 98 17 17 16 17 16 16 15 16 15 15 14 15 14
  //   14 13 14 13 13 12 13 12 3 2 3 2 2 1 2 1 1 0 1 40 0 bf 40 bf bf be bf be be bd be bd bd bc bd bc bc
  //   bb bc bb 9b 9a 9b 9a 9a 99 9a 99 99 98 99 98 98 17 98 17 17 16 17 16 16 15 16 15 15 14 15 14 14 13
  //   14 13 4 3 4 3 3 2 3 2 2 1 2 1 1 0 1 40 0 bf 40 bf bf be bf be be bd be bd bd bc bd bc 9c 9b 9c 9b 9b
  //   9a 9b 9a 9a 99 9a 99 99 98 99 98 98 17 98 17 17 16 17 16 16 15 16 15 15 14 15 14 5 4 5 4 4 3 4 3 3 2
  //   3 2 2 1 2 1 1 0 1 40 0 bf 40 bf bf be bf be be bd be bd 9d 9c 9d 9c 9c 9b 9c 9b 9b 9a 9b 9a 9a 99 9a
  //   99 99 98 99 98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
  //   (unused)
  //   (unused)
endmodule

module Control (
  input  [3:0] NZVC,
  input  [7:0] Opcode,
  output [15:0] CtrlLines,
  output Clk
);

  wire [2:0] Phase_q;

  Clock clock_1 (.out(Clk));
  // Probe on Phase_q
  Counter #(.width(3), .max('h7)) Phase (
    .count(1'b1), .Q(Phase_q), .clk(Clk), .clr(CtrlLines[15]));  // open: load, D, carry
  ROM #(.addrWidth(13)) rom_1 (.addr({NZVC, Phase_q, Opcode[5:0]}), .data(CtrlLines[15:8]));  // open: sel
  ROM #(.addrWidth(13)) rom_2 (.addr({NZVC, Phase_q, Opcode[5:0]}), .data(CtrlLines[7:0]));  // open: sel

  // Other names for the same wires on the sheet: PhaseRst = CtrlLines[15]

  // Notes on the sheet:
  //   contents of rom_1 (hex, n*v repeats v):
  //   64*0 5*19 0 8*19 10 10 19*0 1a 1a d d 25*0 5*80 0 10*80 5*10 14*0 4*80 30*0 20 10*0 5*21 30 30 0 0
  //   20 20 0 20 21 21 0 0 20 20 4*0 70 5*0 61 0 30 21*0 80 15*0 14*80 4*0 80 5*0 80 0 21 32*0 5*80 26*0
  //   80 208*0 5*19 0 8*19 10 10 19*0 1a 1a d d 25*0 5*80 0 10*80 5*10 14*0 4*80 30*0 20 10*0 5*21 30 30 0
  //   0 20 20 0 20 21 21 20 0 80 20 4*0 70 5*0 61 0 30 21*0 80 15*0 14*80 4*0 80 5*0 80 0 21 32*0 5*80
  //   26*0 80 208*0 5*19 0 8*19 10 10 19*0 1a 1a d d 25*0 5*80 0 10*80 5*10 14*0 4*80 30*0 20 10*0 5*21 30
  //   30 0 0 20 20 0 20 21 21 0 20 20 80 4*0 70 5*0 61 0 30 21*0 80 15*0 14*80 4*0 80 5*0 80 0 21 32*0
  //   5*80 26*0 80 208*0 5*19 0 8*19 10 10 19*0 1a 1a d d 25*0 5*80 0 10*80 5*10 14*0 4*80 30*0 20 10*0
  //   5*21 30 30 0 0 20 20 0 20 21 21 20 20 80 80 4*0 70 5*0 61 0 30 21*0 80 15*0 14*80 4*0 80 5*0 80 0 21
  //   32*0 5*80 26*0 80 208*0 5*19 0 8*19 10 10 19*0 1a 1a d d 25*0 5*80 0 10*80 5*10 14*0 4*80 30*0 20
  //   10*0 5*21 30 30 0 20 80 20 20 80 21 21 0 0 20 20 4*0 70 5*0 61 0 30 21*0 80 15*0 14*80 4*0 80 5*0 80
  //   0 21 32*0 5*80 26*0 80 208*0 5*19 0 8*19 10 10 19*0 1a 1a d d 25*0 5*80 0 10*80 5*10 14*0 4*80 30*0
  //   20 10*0 5*21 30 30 0 20 80 20 20 80 21 21 20 0 80 20 4*0 70 5*0 61 0 30 21*0 80 15*0 14*80 4*0 80
  //   5*0 80 0 21 32*0 5*80 26*0 80 208*0 5*19 0 8*19 10 10 19*0 1a 1a d d 25*0 5*80 0 10*80 5*10 14*0
  //   4*80 30*0 20 10*0 5*21 30 30 0 20 80 20 20 80 21 21 0 20 20 80 4*0 70 5*0 61 0 30 21*0 80 15*0 14*80
  //   4*0 80 5*0 80 0 21 32*0 5*80 26*0 80 208*0 5*19 0 8*19 10 10 19*0 1a 1a d d 25*0 5*80 0 10*80 5*10
  //   14*0 4*80 30*0 20 10*0 5*21 30 30 0 20 80 20 20 80 21 21 20 20 80 80 4*0 70 5*0 61 0 30 21*0 80 15*0
  //   14*80 4*0 80 5*0 80 0 21 32*0 5*80 26*0 80 208*0 5*19 0 8*19 10 10 19*0 1a 1a d d 25*0 5*80 0 10*80
  //   5*10 14*0 4*80 30*0 20 10*0 5*21 30 30 20 0 20 80 20 80 21 21 0 0 20 20 4*0 70 5*0 61 0 30 21*0 80
  //   15*0 14*80 4*0 80 5*0 80 0 21 32*0 5*80 26*0 80 208*0 5*19 0 8*19 10 10 19*0 1a 1a d d 25*0 5*80 0
  //   10*80 5*10 14*0 4*80 30*0 20 10*0 5*21 30 30 20 0 20 80 20 80 21 21 20 0 80 20 4*0 70 5*0 61 0 30
  //   21*0 80 15*0 14*80 4*0 80 5*0 80 0 21 32*0 5*80 26*0 80 208*0 5*19 0 8*19 10 10 19*0 1a 1a d d 25*0
  //   5*80 0 10*80 5*10 14*0 4*80 30*0 20 10*0 5*21 30 30 20 0 20 80 20 80 21 21 0 20 20 80 4*0 70 5*0 61
  //   0 30 21*0 80 15*0 14*80 4*0 80 5*0 80 0 21 32*0 5*80 26*0 80 208*0 5*19 0 8*19 10 10 19*0 1a 1a d d
  //   25*0 5*80 0 10*80 5*10 14*0 4*80 30*0 20 10*0 5*21 30 30 20 0 20 80 20 80 21 21 20 20 80 80 4*0 70
  //   5*0 61 0 30 21*0 80 15*0 14*80 4*0 80 5*0 80 0 21 32*0 5*80 26*0 80 208*0 5*19 0 8*19 10 10 19*0 1a
  //   1a d d 25*0 5*80 0 10*80 5*10 14*0 4*80 30*0 20 10*0 5*21 30 30 20 20 80 80 20 80 21 21 0 0 20 20
  //   4*0 70 5*0 61 0 30 21*0 80 15*0 14*80 4*0 80 5*0 80 0 21 32*0 5*80 26*0 80 208*0 5*19 0 8*19 10 10
  //   19*0 1a 1a d d 25*0 5*80 0 10*80 5*10 14*0 4*80 30*0 20 10*0 5*21 30 30 20 20 80 80 20 80 21 21 20 0
  //   80 20 4*0 70 5*0 61 0 30 21*0 80 15*0 14*80 4*0 80 5*0 80 0 21 32*0 5*80 26*0 80 208*0 5*19 0 8*19
  //   10 10 19*0 1a 1a d d 25*0 5*80 0 10*80 5*10 14*0 4*80 30*0 20 10*0 5*21 30 30 20 20 80 80 20 80 21
  //   21 0 20 20 80 4*0 70 5*0 61 0 30 21*0 80 15*0 14*80 4*0 80 5*0 80 0 21 32*0 5*80 26*0 80 208*0 5*19
  //   0 8*19 10 10 19*0 1a 1a d d 25*0 5*80 0 10*80 5*10 14*0 4*80 30*0 20 10*0 5*21 30 30 20 20 80 80 20
  //   80 21 21 20 20 80 80 4*0 70 5*0 61 0 30 21*0 80 15*0 14*80 4*0 80 5*0 80 0 21 32*0 5*80 26*0 80
  //   contents of rom_2 (hex, n*v repeats v):
  //   40*a 5*0 a 0 a 16*0 5*40 12 40 7*80 42 82 19*12 40 80 0 0 12 5*0 12 0 12 21*0 22 10*0 19*22 4*0 22
  //   5*0 22 0 22 21*0 1 10*0 5*4 40 80 0 0 1 1 0 1 4 4 0 0 1 1 4*0 40 5*0 4 0 80 63*0 4 208*0 40*a 5*0 a
  //   0 a 16*0 5*40 12 40 7*80 42 82 19*12 40 80 0 0 12 5*0 12 0 12 21*0 22 10*0 19*22 4*0 22 5*0 22 0 22
  //   21*0 1 10*0 5*4 40 80 0 0 1 1 0 1 4 4 1 0 0 1 4*0 40 5*0 4 0 80 63*0 4 208*0 40*a 5*0 a 0 a 16*0
  //   5*40 12 40 7*80 42 82 19*12 40 80 0 0 12 5*0 12 0 12 21*0 22 10*0 19*22 4*0 22 5*0 22 0 22 21*0 1
  //   10*0 5*4 40 80 0 0 1 1 0 1 4 4 0 1 1 5*0 40 5*0 4 0 80 63*0 4 208*0 40*a 5*0 a 0 a 16*0 5*40 12 40
  //   7*80 42 82 19*12 40 80 0 0 12 5*0 12 0 12 21*0 22 10*0 19*22 4*0 22 5*0 22 0 22 21*0 1 10*0 5*4 40
  //   80 0 0 1 1 0 1 4 4 1 1 6*0 40 5*0 4 0 80 63*0 4 208*0 40*a 5*0 a 0 a 16*0 5*40 12 40 7*80 42 82
  //   19*12 40 80 0 0 12 5*0 12 0 12 21*0 22 10*0 19*22 4*0 22 5*0 22 0 22 21*0 1 10*0 5*4 40 80 0 1 0 1 1
  //   0 4 4 0 0 1 1 4*0 40 5*0 4 0 80 63*0 4 208*0 40*a 5*0 a 0 a 16*0 5*40 12 40 7*80 42 82 19*12 40 80 0
  //   0 12 5*0 12 0 12 21*0 22 10*0 19*22 4*0 22 5*0 22 0 22 21*0 1 10*0 5*4 40 80 0 1 0 1 1 0 4 4 1 0 0 1
  //   4*0 40 5*0 4 0 80 63*0 4 208*0 40*a 5*0 a 0 a 16*0 5*40 12 40 7*80 42 82 19*12 40 80 0 0 12 5*0 12 0
  //   12 21*0 22 10*0 19*22 4*0 22 5*0 22 0 22 21*0 1 10*0 5*4 40 80 0 1 0 1 1 0 4 4 0 1 1 5*0 40 5*0 4 0
  //   80 63*0 4 208*0 40*a 5*0 a 0 a 16*0 5*40 12 40 7*80 42 82 19*12 40 80 0 0 12 5*0 12 0 12 21*0 22
  //   10*0 19*22 4*0 22 5*0 22 0 22 21*0 1 10*0 5*4 40 80 0 1 0 1 1 0 4 4 1 1 6*0 40 5*0 4 0 80 63*0 4
  //   208*0 40*a 5*0 a 0 a 16*0 5*40 12 40 7*80 42 82 19*12 40 80 0 0 12 5*0 12 0 12 21*0 22 10*0 19*22
  //   4*0 22 5*0 22 0 22 21*0 1 10*0 5*4 40 80 1 0 1 0 1 0 4 4 0 0 1 1 4*0 40 5*0 4 0 80 63*0 4 208*0 40*a
  //   5*0 a 0 a 16*0 5*40 12 40 7*80 42 82 19*12 40 80 0 0 12 5*0 12 0 12 21*0 22 10*0 19*22 4*0 22 5*0 22
  //   0 22 21*0 1 10*0 5*4 40 80 1 0 1 0 1 0 4 4 1 0 0 1 4*0 40 5*0 4 0 80 63*0 4 208*0 40*a 5*0 a 0 a
  //   16*0 5*40 12 40 7*80 42 82 19*12 40 80 0 0 12 5*0 12 0 12 21*0 22 10*0 19*22 4*0 22 5*0 22 0 22 21*0
  //   1 10*0 5*4 40 80 1 0 1 0 1 0 4 4 0 1 1 5*0 40 5*0 4 0 80 63*0 4 208*0 40*a 5*0 a 0 a 16*0 5*40 12 40
  //   7*80 42 82 19*12 40 80 0 0 12 5*0 12 0 12 21*0 22 10*0 19*22 4*0 22 5*0 22 0 22 21*0 1 10*0 5*4 40
  //   80 1 0 1 0 1 0 4 4 1 1 6*0 40 5*0 4 0 80 63*0 4 208*0 40*a 5*0 a 0 a 16*0 5*40 12 40 7*80 42 82
  //   19*12 40 80 0 0 12 5*0 12 0 12 21*0 22 10*0 19*22 4*0 22 5*0 22 0 22 21*0 1 10*0 5*4 40 80 1 1 0 0 1
  //   0 4 4 0 0 1 1 4*0 40 5*0 4 0 80 63*0 4 208*0 40*a 5*0 a 0 a 16*0 5*40 12 40 7*80 42 82 19*12 40 80 0
  //   0 12 5*0 12 0 12 21*0 22 10*0 19*22 4*0 22 5*0 22 0 22 21*0 1 10*0 5*4 40 80 1 1 0 0 1 0 4 4 1 0 0 1
  //   4*0 40 5*0 4 0 80 63*0 4 208*0 40*a 5*0 a 0 a 16*0 5*40 12 40 7*80 42 82 19*12 40 80 0 0 12 5*0 12 0
  //   12 21*0 22 10*0 19*22 4*0 22 5*0 22 0 22 21*0 1 10*0 5*4 40 80 1 1 0 0 1 0 4 4 0 1 1 5*0 40 5*0 4 0
  //   80 63*0 4 208*0 40*a 5*0 a 0 a 16*0 5*40 12 40 7*80 42 82 19*12 40 80 0 0 12 5*0 12 0 12 21*0 22
  //   10*0 19*22 4*0 22 5*0 22 0 22 21*0 1 10*0 5*4 40 80 1 1 0 0 1 0 4 4 1 1 6*0 40 5*0 4 0 80 63*0 4
endmodule
