// Logisim project eprocpu.circ as structural Verilog: 4 circuits, main circuit main
module main (
);

  wire Aload, Clk, FlagWr, IRload, MARload, not_1_out, not_2_out, PCcntl, PCload, RAMwrite, SHOload;
  wire [2:0] ALUop;
  wire [3:0] NZVC, Opcode;
  wire [7:0] A_q, ALU_output, Ashow_q, rom_1_data;
  wire [11:0] IRMAR, PC_logic_output;

  // Probe on PC_logic_output
  PClogic PC_logic (.PCctrl(PCcntl), .PCload(PCload), .IRMAR(IRMAR), .Output(PC_logic_output), .Clk(Clk));
  // Probe on Opcode
  // Probe on NZVC
  Control Control (
    .Opcode(Opcode), .NZVC(NZVC), .ALUop(ALUop), .SHOload(SHOload), .RAMwrite(RAMwrite), .FlagWr(FlagWr),
    .Aload(Aload), .MARload(MARload), .IRload(IRload), .PCload(PCload), .PCctrl(PCcntl), .Clk(Clk));
  not not_1 (not_1_out, PC_logic_output[11]);
  not not_2 (not_2_out, RAMwrite);
  ROM #(.addrWidth(11)) rom_1 (.addr(PC_logic_output[10:0]), .data(rom_1_data), .sel(not_1_out));
  RAM #(.addrWidth(11)) ram_1 (
    .addr(PC_logic_output[10:0]), .data(rom_1_data), .sel(PC_logic_output[11]), .clk(Clk), .ld(not_2_out));  // open: clr
  Register IR (.D(rom_1_data), .en(IRload), .Q({Opcode, IRMAR[11:8]}), .clk(Clk));  // open: clr
  // Probe on rom_1_data
  // Probe on IRMAR
  Register MAR (.D(rom_1_data), .en(MARload), .Q(IRMAR[7:0]), .clk(Clk));  // open: clr
  assign rom_1_data = RAMwrite ? ALU_output : 8'bz;  // Controlled_Buffer controlled_buffer_1
  Register A (.D(rom_1_data), .en(Aload), .Q(A_q), .clk(Clk));  // open: clr
  Register Ashow (.D(A_q), .en(SHOload), .Q(Ashow_q), .clk(Clk));  // open: clr
  // Probe on ALUop
  // Probe on ALU_output
  ALU ALU (.Op(ALUop), .Arg1(rom_1_data), .Arg2(A_q), .NZVC(NZVC), .Output(ALU_output), .FlagWr(FlagWr), .Clk(Clk));
  Hex_Digit_Display hex_digit_display_1 (.value(Ashow_q[7:4]));  // open: dp
  Hex_Digit_Display hex_digit_display_2 (.value(Ashow_q[3:0]));  // open: dp

  // Notes on the sheet:
  //   contents of rom_1 (hex, n*v repeats v):
  //   80 1e 78 0 78 1 88 0 78 2 88 1 8 2 c0 1b 88 1 78 0 88 2 e0 0 78 1 90 5 90 1b 1
endmodule

module ALU (
  input  [2:0] Op,
  input  FlagWr,
  input  [7:0] Arg1,
  input  [7:0] Arg2,
  input  Clk,
  output [3:0] NZVC,
  output [7:0] Output
);

  wire Coutlow, Noutlow, Voutlow, Zoutlow;
  wire [3:0] Resultlow;
  wire [7:0] rom_1_data;

  ROM #(.addrWidth(13)) rom_1 (.addr({Op, Arg1[7:4], Arg2[7:4], Zoutlow, Coutlow}), .data(rom_1_data));  // open: sel
  ROM #(.addrWidth(13)) rom_2 (
    .addr({Op, Arg1[3:0], Arg2[3:0], 2'b10}), .data({Noutlow, Zoutlow, Voutlow, Coutlow, Resultlow}));  // open: sel
  Register #(.width(4)) Flags (.D(rom_1_data[7:4]), .en(FlagWr), .Q(NZVC), .clk(Clk));  // open: clr
  Register ALUout (.D({rom_1_data[3:0], Resultlow}), .en(FlagWr), .Q(Output), .clk(Clk));  // open: clr

  // Other names for the same wires on the sheet: Arg2high[3:0] = Arg2[7:4]; Arg1high[3:0] = Arg1[7:4];
  //   Arg2low[3:0] = Arg2[3:0]; Arg1low[3:0] = Arg1[3:0]; ALUop[2:0] = Op

  // Notes on the sheet:
  //   contents of rom_1 (hex, n*v repeats v):
  //   40 1 0 1 1 2 1 2 2 3 2 3 3 4 3 4 4 5 4 5 5 6 5 6 6 7 6 7 7 a8 7 a8 88 89 88 89 89 8a 89 8a 8a 8b 8a
  //   8b 8b 8c 8b 8c 8c 8d 8c 8d 8d 8e 8d 8e 8e 8f 8e 8f 8f 50 8f 10 1 2 1 2 2 3 2 3 3 4 3 4 4 5 4 5 5 6 5
  //   6 6 7 6 7 7 a8 7 a8 a8 a9 a8 a9 89 8a 89 8a 8a 8b 8a 8b 8b 8c 8b 8c 8c 8d 8c 8d 8d 8e 8d 8e 8e 8f 8e
  //   8f 8f 50 8f 10 50 11 10 11 2 3 2 3 3 4 3 4 4 5 4 5 5 6 5 6 6 7 6 7 7 a8 7 a8 a8 a9 a8 a9 a9 aa a9 aa
  //   8a 8b 8a 8b 8b 8c 8b 8c 8c 8d 8c 8d 8d 8e 8d 8e 8e 8f 8e 8f 8f 50 8f 10 50 11 10 11 11 12 11 12 3 4
  //   3 4 4 5 4 5 5 6 5 6 6 7 6 7 7 a8 7 a8 a8 a9 a8 a9 a9 aa a9 aa aa ab aa ab 8b 8c 8b 8c 8c 8d 8c 8d 8d
  //   8e 8d 8e 8e 8f 8e 8f 8f 50 8f 10 50 11 10 11 11 12 11 12 12 13 12 13 4 5 4 5 5 6 5 6 6 7 6 7 7 a8 7
  //   a8 a8 a9 a8 a9 a9 aa a9 aa aa ab aa ab ab ac ab ac 8c 8d 8c 8d 8d 8e 8d 8e 8e 8f 8e 8f 8f 50 8f 10
  //   50 11 10 11 11 12 11 12 12 13 12 13 13 14 13 14 5 6 5 6 6 7 6 7 7 a8 7 a8 a8 a9 a8 a9 a9 aa a9 aa aa
  //   ab aa ab ab ac ab ac ac ad ac ad 8d 8e 8d 8e 8e 8f 8e 8f 8f 50 8f 10 50 11 10 11 11 12 11 12 12 13
  //   12 13 13 14 13 14 14 15 14 15 6 7 6 7 7 a8 7 a8 a8 a9 a8 a9 a9 aa a9 aa aa ab aa ab ab ac ab ac ac
  //   ad ac ad ad ae ad ae 8e 8f 8e 8f 8f 50 8f 10 50 11 10 11 11 12 11 12 12 13 12 13 13 14 13 14 14 15
  //   14 15 15 16 15 16 7 a8 7 a8 a8 a9 a8 a9 a9 aa a9 aa aa ab aa ab ab ac ab ac ac ad ac ad ad ae ad ae
  //   ae af ae af 8f 50 8f 10 50 11 10 11 11 12 11 12 12 13 12 13 13 14 13 14 14 15 14 15 15 16 15 16 16
  //   17 16 17 88 89 88 89 89 8a 89 8a 8a 8b 8a 8b 8b 8c 8b 8c 8c 8d 8c 8d 8d 8e 8d 8e 8e 8f 8e 8f 8f 50
  //   8f 10 70 31 30 31 31 32 31 32 32 33 32 33 33 34 33 34 34 35 34 35 35 36 35 36 36 37 36 37 37 98 37
  //   98 89 8a 89 8a 8a 8b 8a 8b 8b 8c 8b 8c 8c 8d 8c 8d 8d 8e 8d 8e 8e 8f 8e 8f 8f 50 8f 10 50 11 10 11
  //   31 32 31 32 32 33 32 33 33 34 33 34 34 35 34 35 35 36 35 36 36 37 36 37 37 98 37 98 98 99 98 99 8a
  //   8b 8a 8b 8b 8c 8b 8c 8c 8d 8c 8d 8d 8e 8d 8e 8e 8f 8e 8f 8f 50 8f 10 50 11 10 11 11 12 11 12 32 33
  //   32 33 33 34 33 34 34 35 34 35 35 36 35 36 36 37 36 37 37 98 37 98 98 99 98 99 99 9a 99 9a 8b 8c 8b
  //   8c 8c 8d 8c 8d 8d 8e 8d 8e 8e 8f 8e 8f 8f 50 8f 10 50 11 10 11 11 12 11 12 12 13 12 13 33 34 33 34
  //   34 35 34 35 35 36 35 36 36 37 36 37 37 98 37 98 98 99 98 99 99 9a 99 9a 9a 9b 9a 9b 8c 8d 8c 8d 8d
  //   8e 8d 8e 8e 8f 8e 8f 8f 50 8f 10 50 11 10 11 11 12 11 12 12 13 12 13 13 14 13 14 34 35 34 35 35 36
  //   35 36 36 37 36 37 37 98 37 98 98 99 98 99 99 9a 99 9a 9a 9b 9a 9b 9b 9c 9b 9c 8d 8e 8d 8e 8e 8f 8e
  //   8f 8f 50 8f 10 50 11 10 11 11 12 11 12 12 13 12 13 13 14 13 14 14 15 14 15 35 36 35 36 36 37 36 37
  //   37 98 37 98 98 99 98 99 99 9a 99 9a 9a 9b 9a 9b 9b 9c 9b 9c 9c 9d 9c 9d 8e 8f 8e 8f 8f 50 8f 10 50
  //   11 10 11 11 12 11 12 12 13 12 13 13 14 13 14 14 15 14 15 15 16 15 16 36 37 36 37 37 98 37 98 98 99
  //   98 99 99 9a 99 9a 9a 9b 9a 9b 9b 9c 9b 9c 9c 9d 9c 9d 9d 9e 9d 9e 8f 50 8f 10 50 11 10 11 11 12 11
  //   12 12 13 12 13 13 14 13 14 14 15 14 15 15 16 15 16 16 17 16 17 37 98 37 98 98 99 98 99 99 9a 99 9a
  //   9a 9b 9a 9b 9b 9c 9b 9c 9c 9d 9c 9d 9d 9e 9d 9e 9e 9f 9e 9f 40 bf 0 bf bf be bf be be bd be bd bd bc
  //   bd bc bc bb bc bb bb ba bb ba ba b9 ba b9 b9 b8 b9 b8 98 17 98 17 17 16 17 16 16 15 16 15 15 14 15
  //   14 14 13 14 13 13 12 13 12 12 11 12 11 11 50 11 10 1 40 1 0 40 bf 0 bf bf be bf be be bd be bd bd bc
  //   bd bc bc bb bc bb bb ba bb ba ba b9 ba b9 99 98 99 98 98 17 98 17 17 16 17 16 16 15 16 15 15 14 15
  //   14 14 13 14 13 13 12 13 12 12 11 12 11 2 1 2 1 1 40 1 0 40 bf 0 bf bf be bf be be bd be bd bd bc bd
  //   bc bc bb bc bb bb ba bb ba 9a 99 9a 99 99 98 99 98 98 17 98 17 17 16 17 16 16 15 16 15 15 14 15 14
  //   14 13 14 13 13 12 13 12 3 2 3 2 2 1 2 1 1 40 1 0 40 bf 0 bf bf be bf be be bd be bd bd bc bd bc bc
  //   bb bc bb 9b 9a 9b 9a 9a 99 9a 99 99 98 99 98 98 17 98 17 17 16 17 16 16 15 16 15 15 14 15 14 14 13
  //   14 13 4 3 4 3 3 2 3 2 2 1 2 1 1 40 1 0 40 bf 0 bf bf be bf be be bd be bd bd bc bd bc 9c 9b 9c 9b 9b
  //   9a 9b 9a 9a 99 9a 99 99 98 99 98 98 17 98 17 17 16 17 16 16 15 16 15 15 14 15 14 5 4 5 4 4 3 4 3 3 2
  //   3 2 2 1 2 1 1 40 1 0 40 bf 0 bf bf be bf be be bd be bd 9d 9c 9d 9c 9c 9b 9c 9b 9b 9a 9b 9a 9a 99 9a
  //   99 99 98 99 98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
  //   contents of rom_2 (hex, n*v repeats v):
  //   40 1 0 1 1 2 1 2 2 3 2 3 3 4 3 4 4 5 4 5 5 6 5 6 6 7 6 7 7 a8 7 a8 88 89 88 89 89 8a 89 8a 8a 8b 8a
  //   8b 8b 8c 8b 8c 8c 8d 8c 8d 8d 8e 8d 8e 8e 8f 8e 8f 8f 50 8f 10 1 2 1 2 2 3 2 3 3 4 3 4 4 5 4 5 5 6 5
  //   6 6 7 6 7 7 a8 7 a8 a8 a9 a8 a9 89 8a 89 8a 8a 8b 8a 8b 8b 8c 8b 8c 8c 8d 8c 8d 8d 8e 8d 8e 8e 8f 8e
  //   8f 8f 50 8f 10 50 11 10 11 2 3 2 3 3 4 3 4 4 5 4 5 5 6 5 6 6 7 6 7 7 a8 7 a8 a8 a9 a8 a9 a9 aa a9 aa
  //   8a 8b 8a 8b 8b 8c 8b 8c 8c 8d 8c 8d 8d 8e 8d 8e 8e 8f 8e 8f 8f 50 8f 10 50 11 10 11 11 12 11 12 3 4
  //   3 4 4 5 4 5 5 6 5 6 6 7 6 7 7 a8 7 a8 a8 a9 a8 a9 a9 aa a9 aa aa ab aa ab 8b 8c 8b 8c 8c 8d 8c 8d 8d
  //   8e 8d 8e 8e 8f 8e 8f 8f 50 8f 10 50 11 10 11 11 12 11 12 12 13 12 13 4 5 4 5 5 6 5 6 6 7 6 7 7 a8 7
  //   a8 a8 a9 a8 a9 a9 aa a9 aa aa ab aa ab ab ac ab ac 8c 8d 8c 8d 8d 8e 8d 8e 8e 8f 8e 8f 8f 50 8f 10
  //   50 11 10 11 11 12 11 12 12 13 12 13 13 14 13 14 5 6 5 6 6 7 6 7 7 a8 7 a8 a8 a9 a8 a9 a9 aa a9 aa aa
  //   ab aa ab ab ac ab ac ac ad ac ad 8d 8e 8d 8e 8e 8f 8e 8f 8f 50 8f 10 50 11 10 11 11 12 11 12 12 13
  //   12 13 13 14 13 14 14 15 14 15 6 7 6 7 7 a8 7 a8 a8 a9 a8 a9 a9 aa a9 aa aa ab aa ab ab ac ab ac ac
  //   ad ac ad ad ae ad ae 8e 8f 8e 8f 8f 50 8f 10 50 11 10 11 11 12 11 12 12 13 12 13 13 14 13 14 14 15
  //   14 15 15 16 15 16 7 a8 7 a8 a8 a9 a8 a9 a9 aa a9 aa aa ab aa ab ab ac ab ac ac ad ac ad ad ae ad ae
  //   ae af ae af 8f 50 8f 10 50 11 10 11 11 12 11 12 12 13 12 13 13 14 13 14 14 15 14 15 15 16 15 16 16
  //   17 16 17 88 89 88 89 89 8a 89 8a 8a 8b 8a 8b 8b 8c 8b 8c 8c 8d 8c 8d 8d 8e 8d 8e 8e 8f 8e 8f 8f 50
  //   8f 10 70 31 30 31 31 32 31 32 32 33 32 33 33 34 33 34 34 35 34 35 35 36 35 36 36 37 36 37 37 98 37
  //   98 89 8a 89 8a 8a 8b 8a 8b 8b 8c 8b 8c 8c 8d 8c 8d 8d 8e 8d 8e 8e 8f 8e 8f 8f 50 8f 10 50 11 10 11
  //   31 32 31 32 32 33 32 33 33 34 33 34 34 35 34 35 35 36 35 36 36 37 36 37 37 98 37 98 98 99 98 99 8a
  //   8b 8a 8b 8b 8c 8b 8c 8c 8d 8c 8d 8d 8e 8d 8e 8e 8f 8e 8f 8f 50 8f 10 50 11 10 11 11 12 11 12 32 33
  //   32 33 33 34 33 34 34 35 34 35 35 36 35 36 36 37 36 37 37 98 37 98 98 99 98 99 99 9a 99 9a 8b 8c 8b
  //   8c 8c 8d 8c 8d 8d 8e 8d 8e 8e 8f 8e 8f 8f 50 8f 10 50 11 10 11 11 12 11 12 12 13 12 13 33 34 33 34
  //   34 35 34 35 35 36 35 36 36 37 36 37 37 98 37 98 98 99 98 99 99 9a 99 9a 9a 9b 9a 9b 8c 8d 8c 8d 8d
  //   8e 8d 8e 8e 8f 8e 8f 8f 50 8f 10 50 11 10 11 11 12 11 12 12 13 12 13 13 14 13 14 34 35 34 35 35 36
  //   35 36 36 37 36 37 37 98 37 98 98 99 98 99 99 9a 99 9a 9a 9b 9a 9b 9b 9c 9b 9c 8d 8e 8d 8e 8e 8f 8e
  //   8f 8f 50 8f 10 50 11 10 11 11 12 11 12 12 13 12 13 13 14 13 14 14 15 14 15 35 36 35 36 36 37 36 37
  //   37 98 37 98 98 99 98 99 99 9a 99 9a 9a 9b 9a 9b 9b 9c 9b 9c 9c 9d 9c 9d 8e 8f 8e 8f 8f 50 8f 10 50
  //   11 10 11 11 12 11 12 12 13 12 13 13 14 13 14 14 15 14 15 15 16 15 16 36 37 36 37 37 98 37 98 98 99
  //   98 99 99 9a 99 9a 9a 9b 9a 9b 9b 9c 9b 9c 9c 9d 9c 9d 9d 9e 9d 9e 8f 50 8f 10 50 11 10 11 11 12 11
  //   12 12 13 12 13 13 14 13 14 14 15 14 15 15 16 15 16 16 17 16 17 37 98 37 98 98 99 98 99 99 9a 99 9a
  //   9a 9b 9a 9b 9b 9c 9b 9c 9c 9d 9c 9d 9d 9e 9d 9e 9e 9f 9e 9f 40 bf 0 bf bf be bf be be bd be bd bd bc
  //   bd bc bc bb bc bb bb ba bb ba ba b9 ba b9 b9 b8 b9 b8 98 17 98 17 17 16 17 16 16 15 16 15 15 14 15
  //   14 14 13 14 13 13 12 13 12 12 11 12 11 11 50 11 10 1 40 1 0 40 bf 0 bf bf be bf be be bd be bd bd bc
  //   bd bc bc bb bc bb bb ba bb ba ba b9 ba b9 99 98 99 98 98 17 98 17 17 16 17 16 16 15 16 15 15 14 15
  //   14 14 13 14 13 13 12 13 12 12 11 12 11 2 1 2 1 1 40 1 0 40 bf 0 bf bf be bf be be bd be bd bd bc bd
  //   bc bc bb bc bb bb ba bb ba 9a 99 9a 99 99 98 99 98 98 17 98 17 17 16 17 16 16 15 16 15 15 14 15 14
  //   14 13 14 13 13 12 13 12 3 2 3 2 2 1 2 1 1 40 1 0 40 bf 0 bf bf be bf be be bd be bd bd bc bd bc bc
  //   bb bc bb 9b 9a 9b 9a 9a 99 9a 99 99 98 99 98 98 17 98 17 17 16 17 16 16 15 16 15 15 14 15 14 14 13
  //   14 13 4 3 4 3 3 2 3 2 2 1 2 1 1 40 1 0 40 bf 0 bf bf be bf be be bd be bd bd bc bd bc 9c 9b 9c 9b 9b
  //   9a 9b 9a 9a 99 9a 99 99 98 99 98 98 17 98 17 17 16 17 16 16 15 16 15 15 14 15 14 5 4 5 4 4 3 4 3 3 2
  //   3 2 2 1 2 1 1 40 1 0 40 bf 0 bf bf be bf be be bd be bd 9d 9c 9d 9c 9c 9b 9c 9b 9b 9a 9b 9a 9a 99 9a
  //   99 99 98 99 98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
  //   (unused)
  //   (unused)
endmodule

module Control (
  input  [3:0] Opcode,
  input  [3:0] NZVC,
  output [2:0] ALUop,
  output SHOload,
  output RAMwrite,
  output FlagWr,
  output Aload,
  output MARload,
  output IRload,
  output PCload,
  output PCctrl,
  output Clk
);

  wire [1:0] Phase_q;
  wire [7:3] rom_1_data;

  Clock clock_1 (.out(Clk));
  Counter #(.width(2), .max('h3)) Phase (.count(1'b1), .Q(Phase_q), .clk(Clk));  // open: load, D, carry, clr
  ROM #(.addrWidth(10)) rom_1 (.addr({Phase_q, Opcode, NZVC}), .data({rom_1_data, ALUop}));  // open: sel
  ROM #(.addrWidth(10)) rom_2 (
    .addr({Phase_q, Opcode, NZVC}), .data({SHOload, RAMwrite, FlagWr, Aload, MARload, IRload, PCload, PCctrl}));  // open: sel

  // Notes on the sheet:
  //   contents of rom_1 (hex, n*v repeats v):
  //   528*0 16*1 16*2 16*3 16*4 16*5 16*6 16*7 16*0 16*1 16*2 16*3 16*4 16*5 16*6 16*7
  //   contents of rom_2 (hex, n*v repeats v):
  //   256*6 256*a 128*21 16*11 16*3 4*1 4*3 4*1 4*3 8*1 8*3 1 3 1 3 1 3 1 3 1 3 1 3 1 3 1 3 1 1 3 3 1 1 3
  //   3 1 1 3 3 1 1 3 3 16*81 16*1 128*41
endmodule

module PClogic (
  input  PCctrl,
  input  [11:0] IRMAR,
  input  PCload,
  input  Clk,
  output [11:0] Output
);

  wire [11:0] adder_1_out, PC_q;

  Multiplexer #(.width(12), .enable("false")) multiplexer_1 (.in0(PC_q), .in1(IRMAR), .out(Output), .sel(PCctrl));
  Adder #(.width(12)) adder_1 (.a(Output), .b(12'h1), .out(adder_1_out));  // open: cin, cout
  Register #(.width(12)) PC (.D(adder_1_out), .en(PCload), .Q(PC_q), .clk(Clk));  // open: clr
endmodule
